# Fritzing sketch BSB-LAN ESP32-Devkit-v1-30pin (saved by Fritzing 0.9.9b)

parts:
  U1 = ESP32 DEVKIT V1 DOIT [part_number=ESP32S-HiLetgo]
  R1 = Resistor [tolerance=±5% resistance=220 package=THT]
  R2 = Temperature Sensor (Thermistor) [thermistor_type=NTC package=THT]

nets:
  N1: U1.GPIO27, R1.Pin_1, R2.pin_1
  N2: U1.GND, R1.Pin_0

custom parts:
  ESP32 DEVKIT V1 DOIT: 30GPIO Version
